// Logisim project hw6.circ as structural Verilog: 2 circuits, main circuit Counter8
module Counter8 (
  input  CLK,
  output [7:0] CNT
);

  wire and_1_out, and_2_out, and_3_out, and_4_out, and_5_out, and_6_out;

  J_K_Flip_Flop j_k_ff_1 (.J(1'b1), .K(1'b1), .clk(CLK), .Q(CNT[0]));  // open: Qn, preset, reset
  J_K_Flip_Flop j_k_ff_2 (.J(CNT[0]), .K(CNT[0]), .clk(CLK), .Q(CNT[1]));  // open: Qn, preset, reset
  and and_1 (and_1_out, CNT[0], CNT[1]);
  J_K_Flip_Flop j_k_ff_3 (.J(and_1_out), .K(and_1_out), .clk(CLK), .Q(CNT[2]));  // open: Qn, preset, reset
  and and_2 (and_2_out, and_1_out, CNT[2]);
  J_K_Flip_Flop j_k_ff_4 (.J(and_2_out), .K(and_2_out), .clk(CLK), .Q(CNT[3]));  // open: Qn, preset, reset
  and and_3 (and_3_out, and_2_out, CNT[3]);
  J_K_Flip_Flop j_k_ff_5 (.J(and_3_out), .K(and_3_out), .clk(CLK), .Q(CNT[4]));  // open: Qn, preset, reset
  and and_4 (and_4_out, and_3_out, CNT[4]);
  J_K_Flip_Flop j_k_ff_6 (.J(and_4_out), .K(and_4_out), .clk(CLK), .Q(CNT[5]));  // open: Qn, preset, reset
  and and_5 (and_5_out, and_4_out, CNT[5]);
  J_K_Flip_Flop j_k_ff_7 (.J(and_5_out), .K(and_5_out), .clk(CLK), .Q(CNT[6]));  // open: Qn, preset, reset
  and and_6 (and_6_out, and_5_out, CNT[6]);
  J_K_Flip_Flop j_k_ff_8 (.J(and_6_out), .K(and_6_out), .clk(CLK), .Q(CNT[7]));  // open: Qn, preset, reset
endmodule

module test (
);

  wire clock_1_out;
  wire [7:0] counter8_1_cnt;

  Clock clock_1 (.out(clock_1_out));
  Counter8 counter8_1 (.CLK(clock_1_out), .CNT(counter8_1_cnt));
  Hex_Digit_Display hex_digit_display_1 (.value(counter8_1_cnt[7:4]));  // open: dp
  Hex_Digit_Display hex_digit_display_2 (.value(counter8_1_cnt[3:0]));  // open: dp
endmodule
